# Fritzing sketch spires (saved by Fritzing 1.0.3b)
circuit board: 5.69999cm x 6.09999cm
breadboards: 2

parts:
  Nano = Arduino Nano (Rev3.0)
  RE1 = Rotary Encoder [package=THT]
  S5 = SPST Switch [package=switch-spdt_kit]
  VCC1 = 4 x AAA Battery Mount
  LDR = Photocell (LDR) [power=0.25W dark_resistance_@0.01lx=300kΩ light_resistance_@100lx=400Ω luminance=10lx package=THT]
  100uF1 = Electrolytic Capacitor [capacitance=0.1mF voltage=35V package="100 mil [THT, electrolytic]"]
  470nf = Ceramic Capacitor [capacitance=0.47µF voltage=16V package="200 mil [THT, multilayer]"]
  4_7K = Resistor [tolerance=±5% resistance=4.7k power=0.25W package=THT]
  104 = Ceramic Capacitor [capacitance=100nF voltage=16V package="200 mil [THT, multilayer]"]
  AD9833 = female pin header, 7 pins [form="♀ (female)"]
  VL53L0/1XV2 = female pin header, 6 pins [form="♀ (female)"]
  TDA7052A = IC, DIP package, 8 pins [chip_label=IC]
  220 = Resistor [tolerance=±1% resistance=220 power=0.25W package=THT]
  220_2 = Resistor [tolerance=±1% resistance=220 power=0.25W package=THT]
  midi = 3.5mm Audio Jack-wq-pj320b.fzpz [package=audio-jack-3.5mm-smd]
  LED8 = LED - 3mm [color="Red (635nm)" current=0.030A package="3 mm [THT]"]
  1K = Resistor [tolerance=±5% resistance=1k power=0.25W package=THT]
  audio = 3.5mm Audio Jack-wq-pj320b.fzpz [package=audio-jack-3.5mm-smd]
  S6 = SPST Switch [package=switch-spdt_kit]
  104_2 = Ceramic Capacitor [capacitance=0.33n voltage=16V package="200 mil [THT, multilayer]"]
  334 = Film/Foil Capacitor [capacitance=100nF voltage=35V package="7.5mm [THT, pp]"]
  10K = Resistor [tolerance=±5% resistance=4.7k power=0.25W package=THT]

nets (from the breadboard view):
  N1: Nano.D1/TX, 220.Pin_1
  GND: Nano.GND, RE1.GND, RE1.SW-2, AD9833.pin2, VL53L0/1XV2.pin2, midi.pin_4, 1K.Pin_0, 104_2.0
  N2: Nano.D2, LED8.anode
  N3: Nano.D3, RE1.Pin-B
  N4: Nano.D4, RE1.SW-1
  N5: Nano.D6, RE1.Pin-A
  N6: Nano.D7, VL53L0/1XV2.pin6
  N7: Nano.D8, AD9833.pin5
  N8: Nano.D11/MOSI, AD9833.pin3
  N9: Nano.VIN, S5.S
  N10: Nano.5V, 100uF1.+, 104.1, AD9833.pin1, TDA7052A.pin1, 220_2.Pin_1, 10K.Pin_0
  N11: Nano.A5, VL53L0/1XV2.pin3
  N12: Nano.A4, VL53L0/1XV2.pin4
  N13: Nano.3V3, VL53L0/1XV2.pin1, 104_2.1
  N14: Nano.D13/SCK, AD9833.pin4
  N15: S5.P, VCC1.+
  N16: VCC1.-, 100uF1.-, 4_7K.Pin_1, 104.0, AD9833.pin6, TDA7052A.pin3, TDA7052A.pin6, audio.pin_4
  N17: LDR.pin_0, S6.O
  N18: LDR.pin_1, S6.S, 334.+
  N19: 470nf.0, 4_7K.Pin_0, AD9833.pin7
  N20: 470nf.1, TDA7052A.pin2
  N21: TDA7052A.pin5, S6.P
  N22: 220.Pin_0, midi.pin_2
  N23: 220_2.Pin_0, midi.Pin_3
  N24: LED8.cathode, 1K.Pin_1
  N25: audio.pin_2, audio.Pin_3, 334.-, 10K.Pin_1

notes:
  spires v1.0
  AD9833
  VL53L01
  jlcjlcjlcjlc
  blueprint@poetaster.de 2025

custom parts:
  Rotary Encoder: Rotary Encoder with push button
  4 x AAA Battery Mount: A 4 x AAA battery pack (4.8 Volts with recharables)
  3.5mm Audio Jack-wq-pj320b.fzpz: 3.5mm Audio Jack WQP-PJ320B is a SMD jack, dia 1/8 inch, female, right angle and through hole.
